// Logisim project Main.circ as structural Verilog: 5 circuits, main circuit main
module main (
  input  Reset,
  output [3:0] zero,
  output [3:0] t0,
  output [3:0] t1,
  output [3:0] t2,
  output [3:0] t3,
  output [3:0] t4,
  output [3:0] sp
);

  wire ALU_zero, branch_1_branch_2, clock_1_out, Control_alusrc, Control_bneq, Control_branch, Control_jump,
       Control_memread, Control_memtoreg, Control_memwrite, Control_regdst, Control_regwrite;
  wire [2:0] Control_aluop;
  wire [3:0] ALU_output, multiplexer_1_out, multiplexer_3_out, multiplexer_5_out, ram_1_data,
       register_file_1_out_8, register_file_1_out_9;
  wire [7:0] adder_1_out, adder_2_out, bit_extender_1_out, multiplexer_2_out, multiplexer_4_out, register_1_q;
  wire [15:0] rom_1_data;

  Clock clock_1 (.out(clock_1_out));
  Register register_1 (.D(multiplexer_2_out), .en(1'b1), .Q(register_1_q), .clk(clock_1_out), .clr(Reset));
  Adder adder_1 (.a(8'h1), .b(register_1_q), .out(adder_1_out));  // open: cin, cout
  ROM #(.dataWidth(16)) rom_1 (.addr(register_1_q), .data(rom_1_data));  // open: sel
  Multiplexer #(.width(4), .enable("false")) multiplexer_1 (
    .in0(rom_1_data[3:0]), .in1(rom_1_data[7:4]), .out(multiplexer_1_out), .sel(Control_regdst));
  Multiplexer #(.width(8), .enable("false")) multiplexer_2 (
    .in0(multiplexer_4_out), .in1(rom_1_data[11:4]), .out(multiplexer_2_out), .sel(Control_jump));
  contorl_unit Control (
    .in_1(rom_1_data[15:12]), .Jump(Control_jump), .BNEQ(Control_bneq), .Branch(Control_branch),
    .ALUOp(Control_aluop), .ALUSrc(Control_alusrc), .MemWrite(Control_memwrite), .MemtoReg(Control_memtoreg),
    .MemRead(Control_memread), .RegDst(Control_regdst), .RegWrite(Control_regwrite));
  register_file register_file_1 (
    .Src_1(rom_1_data[11:8]), .Src_2(rom_1_data[7:4]), .Write(multiplexer_1_out), .Data(multiplexer_5_out),
    .Clock(clock_1_out), .Reg_Write(Control_regwrite), .zero(zero), .t0(t0), .t1(t1), .t2(t2), .t3(t3),
    .t4(t4), .sp(sp), .out_8(register_file_1_out_8), .out_9(register_file_1_out_9), .Reset(Reset));
  Multiplexer #(.width(4), .enable("false")) multiplexer_3 (
    .in0(register_file_1_out_9), .in1(rom_1_data[3:0]), .out(multiplexer_3_out), .sel(Control_alusrc));
  assign bit_extender_1_out = {{4{rom_1_data[3]}}, rom_1_data[3:0]};  // Bit_Extender bit_extender_1
  ALU ALU (
    .Operand1(register_file_1_out_8), .Operand2(multiplexer_3_out), .Control(Control_aluop), .Zero(ALU_zero),
    .Output(ALU_output));
  Adder adder_2 (.a(adder_1_out), .b(bit_extender_1_out), .out(adder_2_out));  // open: cin, cout
  branch branch_1 (
    .branch(Control_branch), .branch_not_equal(Control_bneq), .zero(ALU_zero), .branch_2(branch_1_branch_2));
  Multiplexer #(.width(8), .enable("false")) multiplexer_4 (
    .in0(adder_1_out), .in1(adder_2_out), .out(multiplexer_4_out), .sel(branch_1_branch_2));
  RAM #(.addrWidth(4), .dataWidth(4), .bus("separate")) ram_1 (
    .addr(ALU_output), .din(register_file_1_out_9), .data(ram_1_data), .str(Control_memwrite), .sel(1'b1),
    .clk(clock_1_out), .ld(Control_memread), .clr(Reset));
  Multiplexer #(.width(4), .enable("false")) multiplexer_5 (
    .in0(ALU_output), .in1(ram_1_data), .out(multiplexer_5_out), .sel(Control_memtoreg));

  // Notes on the sheet:
  //   contents of rom_1 (hex, n*v repeats v):
  //   1001 2024 6213 5343 b245 d251 e241 7212 9112 a512 3241 f324 324 8314 4314 c0a0
endmodule

module contorl_unit (
  input  [3:0] in_1,
  output Jump,
  output BNEQ,
  output Branch,
  output [2:0] ALUOp,
  output ALUSrc,
  output MemWrite,
  output MemtoReg,
  output MemRead,
  output RegDst,
  output RegWrite
);

  ROM #(.addrWidth(4), .dataWidth(12)) rom_1 (
    .addr(in_1), .data({RegDst, Jump, Branch, BNEQ, MemRead, MemtoReg, MemWrite, ALUSrc, ALUOp, RegWrite}));  // open: sel

  // Notes on the sheet:
  //   contents of rom_1 (hex, n*v repeats v):
  //   8d1 1 811 9 902 813 3 817 a02 81b 81d 5 c00 815 7 830
endmodule

module ALU (
  input  [2:0] Control,
  input  [3:0] Operand1,
  input  [3:0] Operand2,
  output [3:0] Output,
  output Zero
);

  wire nor_2_out;
  wire [3:0] adder_1_out, and_1_out, bit_extender_1_out, multiplexer_1_out, multiplexer_2_out, nor_1_out,
       or_1_out, shifter_1_out, shifter_2_out, subtractor_1_out;

  Adder #(.width(4)) adder_1 (.a(Operand1), .b(Operand2), .out(adder_1_out));  // open: cin, cout
  Subtractor #(.width(4)) subtractor_1 (.a(Operand1), .b(Operand2), .out(subtractor_1_out));  // open: bin, bout
  assign and_1_out = Operand1 & Operand2;  // AND_Gate and_1, 4 bits wide
  assign or_1_out = Operand1 | Operand2;  // OR_Gate or_1, 4 bits wide
  assign nor_1_out = ~(Operand1 | Operand2);  // NOR_Gate nor_1, 4 bits wide
  Shifter #(.width(4)) shifter_1 (.in(Operand1), .\dist (Operand2[1:0]), .out(shifter_1_out));
  Shifter #(.width(4), .shift("lr")) shifter_2 (.in(Operand1), .\dist (Operand2[1:0]), .out(shifter_2_out));
  nor nor_2 (nor_2_out, Operand2[2], Operand2[3]);
  assign bit_extender_1_out = {{3{1'b0}}, nor_2_out};  // Bit_Extender bit_extender_1
  Multiplexer #(.width(4), .enable("false")) multiplexer_1 (
    .in0(bit_extender_1_out), .in1(shifter_1_out), .out(multiplexer_1_out), .sel(nor_2_out));
  Multiplexer #(.width(4), .enable("false")) multiplexer_2 (
    .in0(bit_extender_1_out), .in1(shifter_2_out), .out(multiplexer_2_out), .sel(nor_2_out));
  Multiplexer #(.select(3), .width(4), .enable("false")) multiplexer_3 (
    .in0(adder_1_out), .in1(subtractor_1_out), .in2(and_1_out), .in3(or_1_out), .in4(nor_1_out),
    .in5(multiplexer_1_out), .in6(multiplexer_2_out), .in7(multiplexer_2_out), .out(Output), .sel(Control));
  nor nor_3 (Zero, Output[0], Output[1], Output[2], Output[3]);

  // Notes on the sheet:
  //   Creates 0000, in case one of rightmost two bits are 1
  //   This Two Mux selects 0000, if
  //   one of rightmost two bits are 1
  //   Dont Care
endmodule

module register_file (
  input  Reg_Write,
  input  [3:0] Src_1,
  input  [3:0] Src_2,
  input  [3:0] Write,
  input  [3:0] Data,
  input  Clock,
  input  Reset,
  output [3:0] out_8,
  output [3:0] out_9,
  output [3:0] sp,
  output [3:0] zero,
  output [3:0] t0,
  output [3:0] t1,
  output [3:0] t2,
  output [3:0] t3,
  output [3:0] t4
);

  wire and_1_out, and_2_out, and_3_out, and_4_out, and_5_out, and_6_out, decoder_1_out1, decoder_1_out2,
       decoder_1_out3, decoder_1_out4, decoder_1_out5, decoder_1_out6, multiplexer_2_out, multiplexer_3_out;
  wire [3:0] multiplexer_1_out;

  Decoder #(.select(3), .enable("false")) decoder_1 (
    .out1(decoder_1_out1), .out2(decoder_1_out2), .out3(decoder_1_out3), .out4(decoder_1_out4),
    .out5(decoder_1_out5), .out6(decoder_1_out6), .sel(Write[2:0]));  // open: out0, out7
  and and_1 (and_1_out, Reg_Write, decoder_1_out1);
  and and_2 (and_2_out, Reg_Write, decoder_1_out2);
  and and_3 (and_3_out, Reg_Write, decoder_1_out3);
  and and_4 (and_4_out, Reg_Write, decoder_1_out4);
  and and_5 (and_5_out, Reg_Write, decoder_1_out5);
  and and_6 (and_6_out, Reg_Write, decoder_1_out6);
  Multiplexer #(.width(4)) multiplexer_1 (.in0(Data), .in1(4'b1111), .out(multiplexer_1_out), .sel(Reset));  // open: en
  Multiplexer multiplexer_2 (.in0(and_6_out), .in1(1'b1), .out(multiplexer_2_out), .sel(Reset));  // open: en
  Multiplexer multiplexer_3 (.in0(Clock), .in1(Reset), .out(multiplexer_3_out), .sel(Reset));  // open: en
  Register #(.width(4)) u_zero (.en(1'b0), .Q(zero), .clr(Reset));  // open: D, clk
  Register #(.width(4)) u_t0 (.D(Data), .en(and_1_out), .Q(t0), .clk(Clock), .clr(Reset));
  Register #(.width(4)) u_t1 (.D(Data), .en(and_2_out), .Q(t1), .clk(Clock), .clr(Reset));
  Register #(.width(4)) u_t2 (.D(Data), .en(and_3_out), .Q(t2), .clk(Clock), .clr(Reset));
  Register #(.width(4)) u_t3 (.D(Data), .en(and_4_out), .Q(t3), .clk(Clock), .clr(Reset));
  Register #(.width(4)) u_t4 (.D(Data), .en(and_5_out), .Q(t4), .clk(Clock), .clr(Reset));
  Register #(.width(4)) u_sp (
    .D(multiplexer_1_out), .en(multiplexer_2_out), .Q(sp), .clk(multiplexer_3_out));  // open: clr
  Multiplexer #(.select(3), .width(4), .enable("false")) multiplexer_4 (
    .in0(zero), .in1(t0), .in2(t1), .in3(t2), .in4(t3), .in5(t4), .in6(sp), .in7(sp), .out(out_8),
    .sel(Src_1[2:0]));
  Multiplexer #(.select(3), .width(4), .enable("false")) multiplexer_5 (
    .in0(zero), .in1(t0), .in2(t1), .in3(t2), .in4(t3), .in5(t4), .in6(sp), .in7(sp), .out(out_9),
    .sel(Src_2[2:0]));

  // Notes on the sheet:
  //   To initialize $sp to 2^4-1 when reset 0 -> 1
  //   Dont care
  //   Dont care
endmodule

module branch (
  input  branch,
  input  branch_not_equal,
  input  zero,
  output branch_2
);

  wire and_1_out, and_2_out, not_1_out;

  not not_1 (not_1_out, zero);
  and and_1 (and_1_out, branch, zero);
  and and_2 (and_2_out, branch_not_equal, not_1_out);
  or or_1 (branch_2, and_1_out, and_2_out);
endmodule
